// Logisim project Parte b.circ as structural Verilog: 1 circuit, main circuit main
module main (
  input  [3:0] x,
  input  start,
  input  clk,
  output [3:0] z
);

  wire [3:0] adder_1_out, multiplexer_1_out;

  Adder #(.width(4)) adder_1 (.a(z), .b(x), .out(adder_1_out));  // open: cin, cout
  Multiplexer #(.width(4)) multiplexer_1 (
    .in0(adder_1_out), .in1(x), .out(multiplexer_1_out), .sel(start));  // open: en
  Register #(.width(4)) register_1 (.D(multiplexer_1_out), .Q(z), .clk(clk));  // open: en, clr
endmodule
