// Logisim project Práctica_circuitos.circ as structural Verilog: 1 circuit, main circuit main
module main (
  input  [7:0] x,
  input  start,
  input  clk,
  output Ready,
  output [3:0] n__de_bits_en_1
);

  wire [3:0] adder_1_out, multiplexer_2_out;
  wire [7:0] multiplexer_1_out, RegX_q, shifter_1_out;

  Shifter #(.shift("lr")) shifter_1 (.in(RegX_q), .\dist (3'b001), .out(shifter_1_out));
  Multiplexer #(.width(8)) multiplexer_1 (
    .in0(shifter_1_out), .in1(x), .out(multiplexer_1_out), .sel(start));  // open: en
  Adder #(.width(4)) adder_1 (.a(n__de_bits_en_1), .b(4'b0000), .out(adder_1_out), .cin(RegX_q[0]));  // open: cout
  Multiplexer #(.width(4)) multiplexer_2 (
    .in0(adder_1_out), .in1(4'b0000), .out(multiplexer_2_out), .sel(start));  // open: en
  Register RegX (.D(multiplexer_1_out), .Q(RegX_q), .clk(clk));  // open: en, clr
  Register #(.width(4)) RegCnt (.D(multiplexer_2_out), .Q(n__de_bits_en_1), .clk(clk));  // open: en, clr
  // Probe on RegX_q
  // Probe on n__de_bits_en_1
  Comparator comparator_1 (.a(RegX_q), .b({8{1'b0}}), .eq(Ready));  // open: gt, lt
endmodule
